# Fritzing sketch Schaltung_Hauptsteuerung (saved by Fritzing 0.9.3b)
breadboards: 1

parts:
  Hauptsteuerung = Arduino Mega 2560 (Rev3)
  Motortreiber_1 = Pololu A4988 [package=SO16]
  Motortreiber_2 = Pololu A4988 [package=SO16]
  Motortreiber_3 = Pololu A4988 [package=SO16]
  Motor_1 = Stepper Motor - Bipolar
  Motor_2 = Stepper Motor - Bipolar
  Motor_3 = Stepper Motor - Bipolar

nets:
  N1: Hauptsteuerung.D6_PWM, Hauptsteuerung.D47
  N2: Hauptsteuerung.D44, Motortreiber_1.ENABLE
  N3: Hauptsteuerung.D45, Motortreiber_2.ENABLE
  N4: Hauptsteuerung.D46, Motortreiber_3.ENABLE
  GND: Motortreiber_1.GND, Motortreiber_2.GND, Motortreiber_3.GND
  N5: Motortreiber_1.1B, Motor_1.D
  N6: Motortreiber_1.1A, Motor_1.B
  N7: Motortreiber_1.2A, Motor_1.C
  N8: Motortreiber_1.2B, Motor_1.A
  12V: Motortreiber_1.VMOT, Motortreiber_2.VMOT, Motortreiber_3.VMOT
  N9: Motortreiber_2.1B, Motor_2.D
  N10: Motortreiber_2.1A, Motor_2.B
  N11: Motortreiber_2.2A, Motor_2.C
  N12: Motortreiber_2.2B, Motor_2.A
  N13: Motortreiber_3.1B, Motor_3.D
  N14: Motortreiber_3.1A, Motor_3.B
  N15: Motortreiber_3.2A, Motor_3.C
  N16: Motortreiber_3.2B, Motor_3.A
